// Logisim project microless_encoder.circ as structural Verilog: 4 circuits, main circuit main
module main (
  input  A,
  input  B,
  output _0,
  output _1,
  output _2,
  output _3,
  output out_7
);

  wire direction_detector_1_out_3, direction_detector_1_out_4;
  wire [3:0] counter_1__0, counter_2__0;

  Direction_Detector direction_detector_1 (
    .A(A), .B(B), .out_3(direction_detector_1_out_3), .out_4(direction_detector_1_out_4));
  Pull_Resistor pull_resistor_1 (.node(direction_detector_1_out_3));
  Pull_Resistor pull_resistor_2 (.node(direction_detector_1_out_4));
  counter counter_1 (
    .CLK(direction_detector_1_out_3), .CLR(1'b0), ._0(counter_1__0[0]), ._1(counter_1__0[1]),
    ._2(counter_1__0[2]), ._3(counter_1__0[3]));
  Pull_Resistor pull_resistor_3 (.node(direction_detector_1_out_4));
  counter counter_2 (
    .CLK(direction_detector_1_out_4), .CLR(1'b0), ._0(counter_2__0[0]), ._1(counter_2__0[1]),
    ._2(counter_2__0[2]), ._3(counter_2__0[3]));
  Subtractor #(.width(4)) subtractor_1 (
    .a(counter_1__0), .b(counter_2__0), .out({_3, _2, _1, _0}), .bout(out_7));  // open: bin

  // Notes on the sheet:
  //   NUMBER OF TURNS
  //   COUNTER CLOCKWISE
endmodule

module Direction_Detector (
  input  A,
  input  B,
  output out_3,
  output out_4
);

  wire d_ff_1_q, d_ff_1_qn, nand_1_out, nand_2_out, xor_1_out;

  D_Flip_Flop d_ff_1 (.clk(A), .D(B), .Q(d_ff_1_q), .Qn(d_ff_1_qn));  // open: preset, en, reset
  nand nand_1 (nand_1_out, d_ff_1_q, A);
  nand nand_2 (nand_2_out, d_ff_1_qn, A);
  xor xor_1 (xor_1_out, nand_2_out, nand_1_out);
  Pull_Resistor pull_resistor_1 (.node(out_3));
  assign out_3 = xor_1_out ? nand_1_out : 1'bz;  // Controlled_Buffer controlled_buffer_1
  Pull_Resistor pull_resistor_2 (.node(out_4));
  assign out_4 = xor_1_out ? nand_2_out : 1'bz;  // Controlled_Buffer controlled_buffer_2
endmodule

module counter (
  input  CLK,
  input  CLR,
  output _0,
  output _1,
  output _2,
  output _3
);

  wire j_k_ff_1_qn, j_k_ff_2_qn, j_k_ff_3_qn;

  Pull_Resistor pull_resistor_1 (.node(CLR));
  J_K_Flip_Flop j_k_ff_1 (.J(1'b1), .clk(CLK), .K(1'b1), .Q(_0), .Qn(j_k_ff_1_qn), .reset(CLR));  // open: preset, en
  J_K_Flip_Flop j_k_ff_2 (
    .J(1'b1), .clk(j_k_ff_1_qn), .K(1'b1), .Q(_1), .Qn(j_k_ff_2_qn), .reset(CLR));  // open: preset, en
  J_K_Flip_Flop j_k_ff_3 (
    .J(1'b1), .clk(j_k_ff_2_qn), .K(1'b1), .Q(_2), .Qn(j_k_ff_3_qn), .reset(CLR));  // open: preset, en
  J_K_Flip_Flop j_k_ff_4 (.J(1'b1), .clk(j_k_ff_3_qn), .K(1'b1), .Q(_3), .reset(CLR));  // open: Qn, preset, en

  // Notes on the sheet:
  //   OUT
endmodule

module tristate (
  input  in_1,
  input  in_2,
  input  in_3,
  output out_4
);

  wire and_1_out, and_2_out, not_1_out;

  not not_1 (not_1_out, in_2);
  and and_1 (and_1_out, in_1, in_2);
  and and_2 (and_2_out, not_1_out, in_3);
  or or_1 (out_4, and_1_out, and_2_out);
endmodule
